// Logisim project SAP-1.circ as structural Verilog: 6 circuits, main circuit main
module main (
  input  [7:0] in_1,
  input  BUS,
  input  in_3,
  input  in_4,
  output [7:0] DATA_BUS
);

  wire AI, AO, BI, BO, CE, CLK, clock_1_out, CO, EO, II, IO, MI, nCLK, OI, PI, PO, RI, RO, SUB;
  wire [3:0] register_module_3_q0_7, register_module_3_q0_7_2;
  wire [7:0] controlled_buffer_1_out, controlled_buffer_2_out, ram_1_data, REG_A, REG_B,
       register_module_1_r0_7, register_module_2_r0_7;
  wire [11:0] control_logic_unit_1_address;
  wire [15:0] rom_1_data;

  assign controlled_buffer_1_out = RI ? DATA_BUS : 8'bz;  // Controlled_Buffer controlled_buffer_1
  Clock clock_1 (.out(clock_1_out));
  assign controlled_buffer_2_out = MI ? DATA_BUS : 8'bz;  // Controlled_Buffer controlled_buffer_2
  assign controlled_buffer_1_out = MI ? register_module_1_r0_7 : 8'bz;  // Controlled_Buffer controlled_buffer_3
  Clock_Module clock_module_1 (.CLK_IN(clock_1_out), .HLT(in_4), .CLK(CLK), .nCLK(nCLK));
  // Probe on register_module_2_r0_7
  Register_Module register_module_1 (
    .D0_7(controlled_buffer_2_out), .IN(MI), .CLK(CLK), .R0_7(register_module_1_r0_7), .CLR(in_3));  // open: Q0_7, OUT
  RAM ram_1 (.addr(controlled_buffer_1_out), .data(ram_1_data), .clk(CLK), .ld(1'b1), .clr(in_3));  // open: sel
  assign DATA_BUS = RO ? ram_1_data : 8'bz;  // Controlled_Buffer controlled_buffer_4
  Register_Module register_module_2 (
    .D0_7(DATA_BUS), .Q0_7(DATA_BUS), .IN(II), .OUT(IO), .CLK(CLK), .R0_7(register_module_2_r0_7));  // open: CLR
  Control_Logic_Unit control_logic_unit_1 (
    .OPCODE(register_module_2_r0_7), .CLK(nCLK), .OI(OI), .CO(CO), .CE(CE), .MI(MI), .SU(SUB), .RI(RI),
    .RO(RO), .EO(EO), .BO(BO), .II(II), .BI(BI), .IO(IO), .AO(AO), .PI(PI), .PO(PO), .AI(AI),
    .DATA(rom_1_data), .ADDRESS(control_logic_unit_1_address));
  LED led_1 (.in(DATA_BUS[7]));
  LED led_2 (.in(DATA_BUS[6]));
  LED led_3 (.in(DATA_BUS[5]));
  LED led_4 (.in(DATA_BUS[3]));
  LED led_5 (.in(DATA_BUS[4]));
  Hex_Digit_Display hex_digit_display_1 (.value(register_module_3_q0_7_2));  // open: dp
  LED led_6 (.in(DATA_BUS[2]));
  LED led_7 (.in(DATA_BUS[1]));
  LED led_8 (.in(DATA_BUS[0]));
  assign DATA_BUS = BUS ? in_1 : 8'bz;  // Controlled_Buffer controlled_buffer_5
  Hex_Digit_Display hex_digit_display_2 (.value(register_module_3_q0_7));  // open: dp
  Register_Module register_module_3 (
    .D0_7(DATA_BUS), .Q0_7({register_module_3_q0_7_2, register_module_3_q0_7}), .IN(OI), .OUT(1'b1),
    .CLK(CLK), .CLR(in_3));  // open: R0_7
  Register_Module register_module_4 (
    .D0_7(DATA_BUS), .Q0_7(DATA_BUS), .IN(PI), .OUT(PO), .CLK(CLK));  // open: R0_7, CLR
  Program_Counter_Module program_counter_module_1 (.EN(CE), .out_5(DATA_BUS), .CLK(CLK), .CLR(in_3), .OUT(CO));
  Register_Module register_module_5 (
    .D0_7(DATA_BUS), .Q0_7(DATA_BUS), .IN(AI), .OUT(AO), .CLK(CLK), .R0_7(REG_A), .CLR(in_3));
  Register_Module register_module_6 (
    .D0_7(DATA_BUS), .Q0_7(DATA_BUS), .IN(BI), .OUT(BO), .CLK(CLK), .R0_7(REG_B), .CLR(in_3));
  ROM #(.addrWidth(12), .dataWidth(16)) rom_1 (.addr(control_logic_unit_1_address), .data(rom_1_data));  // open: sel
  ALU_Module alu_module_1 (.REG_A(REG_A), .REG_B(REG_B), .EO(EO), .SUB(SUB), .OUT(DATA_BUS));

  // Other names for the same wires on the sheet: BUS_t[7:0] = DATA_BUS; CLR = in_3; HLT = in_4

  // Notes on the sheet:
  //   CLOCK MODULE
  //   MEMORY ADDRESS REGISTER
  //   RANDOM ACCESS MEMORY
  //   INSTRUCTION REGISTER
  //   DATA BUS
  //   CONTROL LOGIC UNIT
  //   OUTPUT REGISTER
  //   PARAMETER REGISTER
  //   PROGRAM COUNTER
  //   A REGISTER
  //   ARITHMATIC LOGIC UNIT
  //   B REGISTER
  //   contents of rom_1 (hex, n*v repeats v):
  //   4001 1802 14*0 4001 1802 4001 1202 4100 1080 10*0 4001 1802 4001 1202 4100 1020 88 9*0 4001 1802
  //   4001 1202 8040
endmodule

module Clock_Module (
  input  CLK_IN,
  input  HLT,
  output CLK,
  output nCLK
);

  wire not_1_out;

  not not_1 (not_1_out, HLT);
  and and_1 (CLK, CLK_IN, not_1_out);
  not not_2 (nCLK, CLK);
endmodule

module Register_Module (
  input  [7:0] D0_7,
  input  IN,
  input  CLK,
  input  OUT,
  input  CLR,
  output [7:0] R0_7,
  output [7:0] Q0_7
);

  wire [7:0] controlled_buffer_1_out;

  assign controlled_buffer_1_out = IN ? D0_7 : 8'bz;  // Controlled_Buffer controlled_buffer_1
  Register register_1 (.D(controlled_buffer_1_out), .en(IN), .Q(R0_7), .clk(CLK), .clr(CLR));
  assign Q0_7 = OUT ? R0_7 : 8'bz;  // Controlled_Buffer controlled_buffer_2
endmodule

module ALU_Module (
  input  [7:0] REG_A,
  input  [7:0] REG_B,
  input  EO,
  input  SUB,
  output [7:0] OUT
);

  wire and_1_out, not_1_out;
  wire [7:0] adder_1_out, controlled_buffer_1_out, controlled_buffer_2_out, controlled_buffer_3_out,
       controlled_buffer_4_out, subtractor_1_out;

  not not_1 (not_1_out, SUB);
  assign controlled_buffer_1_out = not_1_out ? REG_A : 8'bz;  // Controlled_Buffer controlled_buffer_1
  assign controlled_buffer_2_out = not_1_out ? REG_B : 8'bz;  // Controlled_Buffer controlled_buffer_2
  assign controlled_buffer_3_out = SUB ? REG_A : 8'bz;  // Controlled_Buffer controlled_buffer_3
  assign controlled_buffer_4_out = SUB ? REG_B : 8'bz;  // Controlled_Buffer controlled_buffer_4
  Adder adder_1 (.a(controlled_buffer_1_out), .b(controlled_buffer_2_out), .out(adder_1_out));  // open: cin, cout
  Subtractor subtractor_1 (
    .a(controlled_buffer_3_out), .b(controlled_buffer_4_out), .out(subtractor_1_out));  // open: bin, bout
  assign OUT = EO ? adder_1_out : 8'bz;  // Controlled_Buffer controlled_buffer_5
  and and_1 (and_1_out, EO, SUB);
  assign OUT = and_1_out ? subtractor_1_out : 8'bz;  // Controlled_Buffer controlled_buffer_6
endmodule

module Program_Counter_Module (
  input  EN,
  input  CLK,
  input  OUT,
  input  CLR,
  output [7:0] out_5
);

  wire [7:0] counter_1_q;

  Counter counter_1 (.count(EN), .Q(counter_1_q), .clk(CLK), .clr(CLR));  // open: load, D, carry
  assign out_5 = OUT ? counter_1_q : 8'bz;  // Controlled_Buffer controlled_buffer_1
endmodule

module Control_Logic_Unit (
  input  [7:0] OPCODE,
  input  CLK,
  input  [15:0] DATA,
  output [11:0] ADDRESS,
  output CO,
  output CE,
  output SU,
  output EO,
  output BO,
  output BI,
  output AO,
  output AI,
  output PO,
  output IO,
  output PI,
  output II,
  output RO,
  output RI,
  output MI,
  output OI
);

  wire decoder_1_out8, T0, T1, T2, T3, T4, T5, T6, T7;

  Counter #(.width(4), .max('hf)) counter_1 (
    .count(1'b1), .Q(ADDRESS[3:0]), .clk(CLK), .clr(decoder_1_out8));  // open: load, D, carry
  Decoder #(.select(4)) decoder_1 (
    .out0(T0), .out1(T1), .out2(T2), .out3(T3), .out4(T4), .out5(T5), .out6(T6), .out7(T7),
    .out8(decoder_1_out8), .sel(ADDRESS[3:0]), .en(1'b1));  // open: out9, out10, out11, out12, out13, out14, out15

  assign ADDRESS[11:4] = OPCODE;
  assign AI = DATA[7];
  assign AO = DATA[6];
  assign BI = DATA[5];
  assign BO = DATA[4];
  assign CE = DATA[1];
  assign CO = DATA[0];
  assign EO = DATA[3];
  assign II = DATA[11];
  assign IO = DATA[10];
  assign MI = DATA[14];
  assign OI = DATA[15];
  assign PI = DATA[9];
  assign PO = DATA[8];
  assign RI = DATA[13];
  assign RO = DATA[12];
  assign SU = DATA[2];
endmodule
